// Logisim project lab1_2.circ as structural Verilog: 1 circuit, main circuit main
module main (
  input  D,
  input  in_2,
  input  in_3,
  input  in_4,
  input  in_5,
  output Y0,
  output Y1,
  output Y2,
  output Y3,
  output Y4,
  output Y5,
  output Y6,
  output Y7,
  output Y8,
  output Y9,
  output Y10,
  output Y11,
  output Y12,
  output Y13,
  output Y14,
  output Y15
);

  wire not_1_out, not_2_out, not_3_out, not_4_out;

  not not_1 (not_1_out, in_2);
  not not_2 (not_2_out, in_3);
  not not_3 (not_3_out, in_4);
  not not_4 (not_4_out, in_5);
  and and_1 (Y0, D, not_1_out, not_2_out, not_3_out, not_4_out);
  and and_2 (Y1, D, not_1_out, not_2_out, not_3_out, in_5);
  and and_3 (Y2, D, not_1_out, not_2_out, in_4, not_4_out);
  and and_4 (Y3, D, not_1_out, not_2_out, in_4, in_5);
  and and_5 (Y4, D, not_1_out, in_3, not_3_out, not_4_out);
  and and_6 (Y5, D, not_1_out, in_3, not_3_out, in_5);
  and and_7 (Y6, D, not_1_out, in_3, in_4, not_4_out);
  and and_8 (Y7, D, not_1_out, in_3, in_4, in_5);
  and and_9 (Y8, D, in_2, not_2_out, not_3_out, not_4_out);
  and and_10 (Y9, D, in_2, not_2_out, not_3_out, in_5);
  and and_11 (Y10, D, in_2, not_2_out, in_4, not_4_out);
  and and_12 (Y11, D, in_2, not_2_out, in_4, in_5);
  and and_13 (Y12, D, in_2, in_3, not_3_out, not_4_out);
  and and_14 (Y13, D, in_2, in_3, not_3_out, in_5);
  and and_15 (Y14, D, in_2, in_3, in_4, not_4_out);
  and and_16 (Y15, D, in_2, in_3, in_4, in_5);

  // Notes on the sheet:
  //   S2
  //   S3
  //   S1
  //   S0
endmodule
