// Logisim project lab1_3.circ as structural Verilog: 1 circuit, main circuit main
module main (
  input  D0,
  input  D1,
  input  D2,
  input  D3,
  input  D4,
  input  D5,
  input  D6,
  input  D7,
  input  D8,
  input  D9,
  input  D10,
  input  D11,
  input  D12,
  input  D13,
  input  D14,
  input  D15,
  input  in_17,
  input  in_18,
  input  in_19,
  input  in_20,
  input  S7,
  input  S6,
  input  S5,
  input  S4,
  output Y0,
  output Y1,
  output Y2,
  output Y3,
  output Y4,
  output Y5,
  output Y6,
  output Y7,
  output Y8,
  output Y9,
  output Y10,
  output Y11,
  output Y12,
  output Y13,
  output Y14,
  output Y15
);

  wire and_1_out, and_2_out, and_3_out, and_4_out, and_5_out, and_6_out, and_7_out, and_8_out, and_9_out,
       and_10_out, and_11_out, and_12_out, and_13_out, and_14_out, and_15_out, and_16_out, not_1_out,
       not_2_out, not_3_out, not_4_out, not_5_out, not_6_out, not_7_out, not_8_out, or_1_out;

  not not_1 (not_1_out, in_17);
  not not_2 (not_2_out, in_18);
  not not_3 (not_3_out, in_19);
  not not_4 (not_4_out, in_20);
  and and_1 (and_1_out, D0, not_1_out, not_2_out, not_3_out, not_4_out);
  and and_2 (and_2_out, D1, not_1_out, not_2_out, not_3_out, in_20);
  and and_3 (and_3_out, D2, not_1_out, not_2_out, in_19, not_4_out);
  and and_4 (and_4_out, D3, not_1_out, not_2_out, in_19, in_20);
  and and_5 (and_5_out, D8, in_17, not_2_out, not_3_out, not_4_out);
  and and_6 (and_6_out, D9, in_17, not_2_out, not_3_out, in_20);
  and and_7 (and_7_out, D10, in_17, not_2_out, in_19, not_4_out);
  and and_8 (and_8_out, D11, in_17, not_2_out, in_19, in_20);
  and and_9 (and_9_out, D4, not_1_out, in_18, not_3_out, not_4_out);
  and and_10 (and_10_out, D5, not_1_out, in_18, not_3_out, in_20);
  and and_11 (and_11_out, D6, not_1_out, in_18, in_19, not_4_out);
  and and_12 (and_12_out, D7, not_1_out, in_18, in_19, in_20);
  and and_13 (and_13_out, D12, in_17, in_18, not_3_out, not_4_out);
  and and_14 (and_14_out, D13, in_17, in_18, not_3_out, in_20);
  and and_15 (and_15_out, D14, in_17, in_18, in_19, not_4_out);
  and and_16 (and_16_out, D15, in_17, in_18, in_19, in_20);
  or or_1 (or_1_out, and_1_out, and_2_out, and_3_out, and_4_out, and_9_out, and_10_out, and_11_out, and_12_out, and_5_out, and_6_out, and_7_out, and_8_out, and_13_out, and_14_out, and_15_out, and_16_out);
  not not_5 (not_5_out, S7);
  not not_6 (not_6_out, S6);
  not not_7 (not_7_out, S5);
  not not_8 (not_8_out, S4);
  and and_17 (Y0, or_1_out, not_5_out, not_6_out, not_7_out, not_8_out);
  and and_18 (Y1, or_1_out, not_5_out, not_6_out, not_7_out, S4);
  and and_19 (Y2, or_1_out, not_5_out, not_6_out, S5, not_8_out);
  and and_20 (Y3, or_1_out, not_5_out, not_6_out, S5, S4);
  and and_21 (Y4, or_1_out, not_5_out, S6, not_7_out, not_8_out);
  and and_22 (Y5, or_1_out, not_5_out, S6, not_7_out, S4);
  and and_23 (Y6, or_1_out, not_5_out, S6, S5, not_8_out);
  and and_24 (Y7, or_1_out, not_5_out, S6, S5, S4);
  and and_25 (Y8, or_1_out, S7, not_6_out, not_7_out, not_8_out);
  and and_26 (Y9, or_1_out, S7, not_6_out, not_7_out, S4);
  and and_27 (Y10, or_1_out, S7, not_6_out, S5, not_8_out);
  and and_28 (Y11, or_1_out, S7, not_6_out, S5, S4);
  and and_29 (Y12, or_1_out, S7, S6, not_7_out, not_8_out);
  and and_30 (Y13, or_1_out, S7, S6, not_7_out, S4);
  and and_31 (Y14, or_1_out, S7, S6, S5, not_8_out);
  and and_32 (Y15, or_1_out, S7, S6, S5, S4);

  // Notes on the sheet:
  //   S3
  //   S1
  //   S2
  //   S0
endmodule
