// Logisim project encoder-decoder.circ as structural Verilog: 1 circuit, main circuit main
module main (
  input  D0,
  input  D1,
  input  D2,
  input  D3,
  input  D4,
  input  D5,
  input  D6,
  input  D7,
  input  D8,
  input  D9
);

  wire and_1_out, and_2_out, and_3_out, and_4_out, and_5_out, and_6_out, and_7_out, and_8_out, and_9_out,
       and_10_out, and_11_out, and_12_out, and_13_out, and_14_out, and_15_out, and_16_out, and_17_out,
       and_18_out, and_19_out, and_20_out, and_21_out, and_22_out, and_23_out, not_1_out, not_2_out,
       not_3_out, or_1_out, or_2_out, or_3_out, or_4_out, or_5_out, or_6_out, or_7_out, or_8_out, or_9_out,
       or_10_out, or_11_out, or_12_out;

  and and_1 (and_1_out, or_2_out, not_3_out);
  or or_1 (or_1_out, D8, D9);
  or or_2 (or_2_out, D4, D5, D6, D7);
  or or_3 (or_3_out, D2, D3, D6, D7);
  or or_4 (or_4_out, D1, D3, D5, D7, D9);
  and and_2 (and_2_out, or_2_out, not_2_out);
  and and_3 (and_3_out, not_1_out, or_3_out);
  not not_1 (not_1_out, or_2_out);
  not not_2 (not_2_out, or_3_out);
  not not_3 (not_3_out, or_4_out);
  and and_4 (and_4_out, or_2_out, not_2_out);
  and and_5 (and_5_out, or_2_out, not_3_out);
  and and_6 (and_6_out, not_2_out, not_3_out);
  and and_7 (and_7_out, or_3_out, not_3_out);
  and and_8 (and_8_out, not_1_out, not_3_out);
  and and_9 (and_9_out, or_3_out, or_4_out);
  and and_10 (and_10_out, not_2_out, not_3_out);
  and and_11 (and_11_out, not_1_out, or_3_out);
  and and_12 (and_12_out, not_1_out, not_3_out);
  and and_13 (and_13_out, or_3_out, not_3_out);
  and and_14 (and_14_out, or_2_out, not_2_out, or_4_out);
  or or_5 (or_5_out, D0, or_1_out, or_2_out, or_3_out, or_4_out);
  or or_6 (or_6_out, or_1_out, and_3_out, and_2_out, and_1_out);
  or or_7 (or_7_out, and_4_out, and_5_out, and_6_out, or_1_out);
  or or_8 (or_8_out, and_7_out, and_8_out);
  or or_9 (or_9_out, or_1_out, or_3_out, and_15_out, and_16_out);
  and and_15 (and_15_out, or_2_out, or_4_out);
  and and_16 (and_16_out, not_1_out, not_3_out);
  or or_10 (or_10_out, not_1_out, and_9_out, and_10_out);
  or or_11 (or_11_out, or_2_out, not_2_out, or_4_out);
  or or_12 (or_12_out, or_1_out, and_11_out, and_12_out, and_13_out, and_14_out);
  and and_17 (and_17_out, or_5_out, or_6_out);
  and and_18 (and_18_out, or_5_out, or_7_out);
  and and_19 (and_19_out, or_5_out, or_8_out);
  and and_20 (and_20_out, or_5_out, or_9_out);
  and and_21 (and_21_out, or_5_out, or_10_out);
  and and_22 (and_22_out, or_5_out, or_11_out);
  and and_23 (and_23_out, or_5_out, or_12_out);
  _7_Segment_Display u_7_segment_display_1 (
    .g(and_17_out), .f(and_18_out), .a(and_20_out), .b(and_21_out), .e(and_19_out), .d(and_23_out),
    .c(and_22_out));  // open: dp

  // Notes on the sheet:
  //   A
  //   B
  //   C
  //   D
  //   f
  //   g
  //   e
  //   a
  //   b
  //   c
  //   d
endmodule
